# Fritzing sketch 7Seg-5011AS (saved by Fritzing 0.9.3b)
breadboards: 1

parts:
  7_Segment1 = 7 Segment Display
  R1 = Resistor [tolerance=±5% resistance=220 package=THT]
  R2 = Resistor [tolerance=±5% resistance=220 package=THT]
  R3 = Resistor [tolerance=±5% resistance=220 package=THT]
  R4 = Resistor [tolerance=±5% resistance=220 package=THT]
  R5 = Resistor [tolerance=±5% resistance=220 package=THT]
  R6 = Resistor [tolerance=±5% resistance=220 package=THT]
  R7 = Resistor [tolerance=±5% resistance=220 package=THT]
  R8 = Resistor [tolerance=±5% resistance=220 package=THT]
  Parça1 = Arduino Uno (Rev3)

nets:
  N1: 7_Segment1.Segment_E, R5.Pin_0
  N2: 7_Segment1.Segment_D, R4.Pin_0
  N3: 7_Segment1.common_cathode, Parça1.GND
  N4: 7_Segment1.Segment_C, R3.Pin_0
  N5: 7_Segment1.Segment_DP, R8.Pin_0
  N6: 7_Segment1.Segment_B, R2.Pin_0
  N7: 7_Segment1.Segment_A, R1.Pin_0
  N8: 7_Segment1.Segment_F, R6.Pin_0
  N9: 7_Segment1.Segment_G, R7.Pin_0
  N10: R1.Pin_1, Parça1.D4
  N11: R2.Pin_1, Parça1.D5_PWM
  N12: R3.Pin_1, Parça1.D6_PWM
  N13: R4.Pin_1, Parça1.D7
  N14: R5.Pin_1, Parça1.D8
  N15: R6.Pin_1, Parça1.D9_PWM
  N16: R7.Pin_1, Parça1.D10_PWM/SS
  N17: R8.Pin_1, Parça1.D11_PWM/MOSI
